# Fritzing sketch PCB_design (saved by Fritzing 0.9.3b)
circuit board: 9.50095cm x 5.96566cm

parts:
  VCC1 = Battery
  R1 = Resistor [tolerance=±5% resistance=220 package="0603 [SMD]"]
  R8 = Resistor [tolerance=±5% resistance=220 package="0603 [SMD]"]
  R4 = Resistor [tolerance=±5% resistance=220 package="0603 [SMD]"]
  R3 = Resistor [tolerance=±5% resistance=220 package="0603 [SMD]"]
  2 = smd LED [color="Red (633nm)" package="0603 [SMD]"]
  1 = smd LED [color="Red (633nm)" package="0603 [SMD]"]
  0 = smd LED [color="Red (633nm)" package="0603 [SMD]"]
  active = smd LED [color="Green (565nm)" package="0603 [SMD]"]
  U2 = RJ45 Jack [package=rj45-8]
  U1 = RJ45 Jack [package=rj45-8]
  Part1 = ATTiny4313 [chip_label=IC package=SO(w)]
  Tick = Pushbutton [package="[SMD]"]
  Phase = Pushbutton [package="[SMD]"]
  Error = Pushbutton [package="[SMD]"]
  Swap = Pushbutton [package="[SMD]"]
  Tick_2 = Pushbutton [package="[SMD]"]
  Read = Pushbutton [package="[SMD]"]

nets:
  N1: VCC1.-, R1.Pin_0, R4.Pin_1, Part1.10, Tick.Pin_3, Tick.Pin_4, Phase.Pin_3, Phase.Pin_4, Error.Pin_3, Error.Pin_4, Swap.Pin_1, Swap.Pin_2, Tick_2.Pin_1, Tick_2.Pin_2, Read.Pin_3, Read.Pin_4
  N2: R1.Pin_1, 2.cathode, 1.cathode, 0.cathode
  N3: R8.Pin_0, R8.Pin_1, U2.3, Part1.4
  N4: R4.Pin_0, active.cathode
  N5: R3.Pin_0, Part1.5
  N6: R3.Pin_1, U1.3
  N7: 2.anode, Part1.14
  N8: 1.anode, Part1.15
  N9: 0.anode, Part1.16
  N10: active.anode, Part1.13
  N11: U2.1, Part1.3
  N12: U2.2, Part1.1
  N13: U2.4, Part1.20
  N14: U2.5, Part1.17
  N15: U2.6, Part1.19
  N16: U2.8, Part1.18
  N17: U1.1, Part1.12
  N18: Part1.2, Tick_2.Pin_3, Tick_2.Pin_4
  N19: Part1.6, Swap.Pin_3, Swap.Pin_4
  N20: Part1.7, Error.Pin_1, Error.Pin_2
  N21: Part1.8, Phase.Pin_1, Phase.Pin_2
  N22: Part1.9, Tick.Pin_1, Tick.Pin_2
  N23: Part1.11, Read.Pin_1, Read.Pin_2

custom parts:
  Pushbutton: A generic pushbutton.
